# Fritzing sketch Commander_SwitchOff_Atmega328 (saved by Fritzing 0.9.3b)
circuit board: 11.4538cm x 8.62224cm
breadboards: 1

parts:
  Relay_1 = Relay T73
  U1 = TLP621 [package=THT]
  D13 = Resistor [tolerance=±5% resistance=220 package=THT]
  Q17 = NPN-Transistor [package="TO92 [THT]"]
  R40 = Resistor [tolerance=±5% resistance=4.7k package=THT]
  Relay_2 = Relay T73
  U2 = TLP621 [package=THT]
  D14 = Resistor [tolerance=±5% resistance=220 package=THT]
  Q18 = NPN-Transistor [package="TO92 [THT]"]
  R41 = Resistor [tolerance=±5% resistance=4.7k package=THT]
  R42 = Resistor [tolerance=±5% resistance=4.7k package=THT]
  R43 = Resistor [tolerance=±5% resistance=4.7k package=THT]
  LED14 = LED - 5mm [color="Red (633nm)" package="5 mm [THT]"]
  LED15 = LED - 5mm [color="Red (633nm)" package="5 mm [THT]"]
  J27 = screw terminal, 2 pins
  7805 = Voltage Regulator [package=to-220-alt]
  R53 = Resistor [tolerance=±5% resistance=4.7k package=THT]
  LED19 = LED - 5mm [color="Red (633nm)" package="5 mm [THT]"]
  R54 = Resistor [tolerance=±5% resistance=4.7k package=THT]
  U6 = atmega328 [package=dip]
  J31 = screw terminal, 2 pins
  R55 = Resistor [tolerance=±5% resistance=4.7k package=THT]
  R57 = Resistor [tolerance=±5% resistance=4.7k package=THT]
  C1 = Ceramic Capacitor [capacitance="100 nF" package="100 mil [THT, multilayer]"]
  XTAL2 = Crystal [frequency="16 Mhz" package=THT]
  C2 = Ceramic Capacitor [capacitance="100 nF" package="100 mil [THT, multilayer]"]
  R58 = Resistor [tolerance=±5% resistance=4.7k package=THT]
  J32 = screw terminal, 2 pins
  R59 = Resistor [tolerance=±5% resistance=4.7k package=THT]
  J33 = screw terminal, 3 pins
  J36 = rounded female pin header, 2 pins [form="♀ (female rounded)"]
  J37 = rounded female pin header, 4 pins [form="♀ (female rounded)"]
  J38 = screw terminal, 2 pins
  R60 = Resistor [tolerance=±5% resistance=4.7k package=THT]
  J34 = rounded female pin header, 3 pins [form="♀ (female rounded)"]
  R61 = Resistor [tolerance=±5% resistance=4.7k package=THT]
  R62 = Resistor [tolerance=±5% resistance=4.7k package=THT]
  Q19 = NPN-Transistor [package="TO92 [THT]"]
  R63 = Resistor [tolerance=±5% resistance=4.7k package=THT]

nets:
  N1: Relay_1.C1, Relay_1.NO, U1.Pin_4, D13.Pin_0, Relay_2.NO, 7805.IN, R53.Pin_1, R54.Pin_1, R55.Pin_1, R60.Pin_0
  N2: Relay_1.C2, D13.Pin_1, Q17.C
  N3: Relay_1.COM, J38.pin1
  GND: Relay_1.NC, Q17.E, Relay_2.NC, Q18.E, J27.pin2, 7805.GND, LED19.cathode, U6.GND, J31.pin2, R55.Pin_0, R57.Pin_1, C1.1, C2.0, J32.pin2, J33.pin1, Q19.E, R63.Pin_1
  N4: U1.Pin_1, R42.Pin_0
  N5: U1.Pin_2, LED14.anode
  N6: U1.Pin_3, R40.Pin_1
  N7: Q17.B, R40.Pin_0
  N8: Relay_2.C1, U2.Pin_4, D14.Pin_0
  N9: Relay_2.C2, D14.Pin_1, Q18.C
  N10: Relay_2.COM, J38.pin2
  N11: U2.Pin_1, R43.Pin_0
  N12: U2.Pin_2, LED15.anode
  N13: U2.Pin_3, R41.Pin_1
  N14: Q18.B, R41.Pin_0
  N15: R42.Pin_1, R43.Pin_1, 7805.OUT, U6.VCC, U6.AVCC, U6.AREF, J31.pin1, R57.Pin_0, R58.Pin_1, J33.pin2
  N16: LED14.cathode, U6.D3_(PWM)
  N17: LED15.cathode, U6.D4
  N18: J27.pin1, R53.Pin_0
  N19: LED19.anode, R54.Pin_0
  N20: U6.RESET, R58.Pin_0
  N21: U6.D0_(RX), J36.pin1
  N22: U6.D1_(TX), J36.pin2
  N23: U6.D2, J33.pin3
  N24: U6.XLAT1, C1.0, XTAL2.pin_0
  N25: U6.XLAT2, XTAL2.pin_1, C2.1
  N26: U6.D5_(PWM), J37.pin1
  N27: U6.D6_(PWM), J37.pin2
  N28: U6.D7, J37.pin3
  N29: U6.D8, J37.pin4
  N30: U6.D9_(PWM), R59.Pin_0
  N31: U6.D10_(PWM), J34.pin3
  N32: U6.D11_(PWM), J34.pin2
  N33: U6.D12, J34.pin1
  N34: U6.D13, R61.Pin_1
  N35: U6.A0, J32.pin1, R59.Pin_1
  N36: U6.A1, R60.Pin_1, R62.Pin_0
  N37: R61.Pin_0, Q19.B, R63.Pin_0
  N38: R62.Pin_1, Q19.C

notes:
  Krishna
  Commander

custom parts:
  Relay T73: An T73 Mini PCB Relay
