# Fritzing sketch Motor (saved by Fritzing 0.9.3b)
circuit board: 18.5cm x 9.27648cm
breadboards: 1

parts:
  U3 = atmega328 [package=dip]
  D4 = Resistor [tolerance=±5% resistance=220 part_number=D_4148 package=THT]
  +_- = LED - 5mm [color="Red (633nm)" part_number=LED1 package="5 mm [THT]"]
  +_-_2 = LED - 5mm [color="Red (633nm)" package="5 mm [THT]"]
  D1 = Resistor [tolerance=±5% resistance=4.7k part_number=Diode_5822_3A package=THT]
  C4 = Capacitor Polarized [package=cpol-radial-1000uf-25v]
  R21 = Resistor [tolerance=±5% resistance=1k package=THT]
  R17 = Resistor [tolerance=±5% resistance=10k package=THT]
  J58 = rounded female pin header, 3 pins [form="♀ (female rounded)"]
  XTAL = Crystal [frequency="16 Mhz" package=THT]
  R2 = Resistor [tolerance=±5% resistance=100 package=THT]
  Q5 = NPN-Transistor [part_number=2N2222A package="TO92 [THT]"]
  R15 = Resistor [tolerance=±5% resistance=1k package=THT]
  Q2 = NPN-Transistor [package="TO92 [THT]"]
  C6 = Ceramic Capacitor [capacitance=22pF package="100 mil [THT, multilayer]"]
  C5 = Ceramic Capacitor [capacitance=22pF package="100 mil [THT, multilayer]"]
  RL1 = OMRON PCB Power Relay – G5LE [part_number="G5LE-1\n" package=THT]
  D5 = Resistor [tolerance=±5% resistance=220 part_number=D_4148 package=THT]
  Q6 = NPN-Transistor [part_number=2N2222A package="TO92 [THT]"]
  R19 = Resistor [tolerance=±5% resistance=1k package=THT]
  R20 = Resistor [tolerance=±5% resistance=1k package=THT]
  +_-_3 = LED - 5mm [color="Red (633nm)" package="5 mm [THT]"]
  U2 = Voltage Regulator - Variable [part_number=LM317 package="TO220 [THT]"]
  U1 = Voltage Regulator - Variable [part_number=LM317 package="TO220 [THT]"]
  - = screw terminal, 2 pins
  R9 = Resistor [tolerance=±5% resistance=820 package=THT]
  R3 = Resistor [tolerance=±5% resistance=390 package=THT]
  R5 = Resistor [tolerance=±5% resistance=1.8k package=THT]
  C1 = Resistor [tolerance=±5% resistance=220 part_number="0.47uF Cap" package=THT]
  D3 = DIODE-ZENER [part_number=D_5819 package=diode-zener]
  R10 = Resistor [tolerance=±5% resistance=370 package=THT]
  R1 = Resistor [tolerance=±5% resistance=1k package=THT]
  C7 = Ceramic Capacitor [capacitance="100 nF" package="100 mil [THT, multilayer]"]
  D2 = Resistor [tolerance=±5% resistance=4.7k part_number=Diode_5822_3A package=THT]
  C3 = Ceramic Capacitor [capacitance="100 nF" package="100 mil [THT, multilayer]"]
  R4 = Resistor [tolerance=±5% resistance=10 part_number=4.5W package=THT]
  G1 = Graetz Bridge Rectifier [package="DIP (Dual Inline) [THT]"]
  C10 = Electrolytic Capacitor [capacitance=33µF voltage=25V package="100 mil [THT, electrolytic]"]
  RL2 = OMRON PCB Power Relay – G5LE [part_number="G5LE-1\n" package=THT]
  C11 = Electrolytic Capacitor [capacitance=33µF voltage=25V package="100 mil [THT, electrolytic]"]
  R13 = Resistor [tolerance=±5% resistance=1k package=THT]
  R14 = Resistor [tolerance=±5% resistance=1k package=THT]
  JP2 = Header 4 [package=jst-4-pth]
  R16 = Resistor [tolerance=±5% resistance=1k package=THT]
  C9 = Ceramic Capacitor [capacitance="100 nF" package="100 mil [THT, multilayer]"]
  C8 = Ceramic Capacitor [capacitance="100 nF" package="100 mil [THT, multilayer]"]
  Q10 = MOSFET-NCHANNEL [package=sot23-3]
  Q4 = Sharp PC817 [package=THT]
  R12 = Resistor [tolerance=±5% resistance=1k package=THT]
  R_Y = screw terminal, 2 pins
  TRF = Header 3 [package=jst-3-pth]
  TRF_2 = Header 2 [package=jst-2-pth]
  C2 = Capacitor Polarized [package=cpol-radial-1000uf-25v]
  JP1 = Header 2 [package=jst-2-pth]
  R7 = Resistor [tolerance=±5% resistance=10k package=THT]
  R6 = Resistor [tolerance=±5% resistance=10k package=THT]
  JP1_2 = Header 2 [package=jst-2-pth]
  Q1 = NPN-Transistor [part_number=2N2222A package="TO92 [THT]"]
  R8 = Resistor [tolerance=±5% resistance=1k package=THT]
  R11 = Resistor [tolerance=±5% resistance=1k package=THT]
  R22 = Resistor [tolerance=±5% resistance=56k package=THT]
  R23 = Resistor [tolerance=±5% resistance=56k package=THT]
  R25 = Resistor [tolerance=±5% resistance=56k package=THT]
  R27 = Resistor [tolerance=±5% resistance=56k package=THT]
  R29 = Resistor [tolerance=±5% resistance=56k package=THT]
  R24 = Resistor [tolerance=±5% resistance=56k package=THT]
  R26 = Resistor [tolerance=±5% resistance=22k package=THT]
  R28 = Resistor [tolerance=±5% resistance=22k package=THT]
  M1 = V18ZA2P [package=v18za2p]
  M2 = V18ZA2P [package=v18za2p]
  D6 = Diode [package=diode-1n4001]
  D7 = Diode [package=diode-1n4001]
  C_START_STOP = screw terminal, 3 pins
  SIM800L_20MM1 = SIM800L_20MM
  JP2_2 = Header 4 [package=jst-4-pth]
  B_Y_R = screw terminal, 3 pins
  Q3 = Sharp PC817 [package=THT]
  Q7 = Sharp PC817 [package=THT]
  Q8 = Sharp PC817 [package=THT]
  Q9 = Sharp PC817 [package=THT]
  J48 = rounded female pin header, 2 pins [form="♀ (female rounded)"]
  RESET1 = Pushbutton [package="[THT]"]
  ON/OFF = SWITCH-DPDT [package=os]

nets:
  N1: U3.RESET, R17.Pin_1, RESET1.Pin_1, RESET1.Pin_2
  N2: U3.D0_(RX), SIM800L_20MM1.PIN_5, J48.pin1
  N3: U3.D1_(TX), SIM800L_20MM1.PIN_4, J48.pin2
  N4: U3.D2, R16.Pin_0
  N5: U3.D3_(PWM), R15.Pin_1
  N6: U3.VCC, U3.AVCC, U3.AREF, D4.Pin_0, C4.+, R17.Pin_0, RL1.COIL2, D5.Pin_1, R19.Pin_1, U1.OUT, R10.Pin_0, C7.1, C3.1, RL2.COIL1, C9.0, C8.1, Q4.Pin_4, SIM800L_20MM1.PIN2, Q3.Pin_3
  N7: U3.GND, C4.-, R2.Pin_1, Q5.E, Q2.E, C6.0, C5.1, Q6.E, R9.Pin_1, R5.Pin_1, C1.Pin_1, R1.Pin_0, C7.0, C3.0, C10.-, C11.-, C9.1, C8.0, R6.Pin_1, SIM800L_20MM1.PIN_6, Q7.Pin_3, Q8.Pin_3, Q9.Pin_2, Q9.Pin_3, RESET1.Pin_3, RESET1.Pin_4, ON/OFF.3, ON/OFF.6
  N8: U3.XLAT1, XTAL.pin_0, C5.0
  N9: U3.XLAT2, XTAL.pin_1, C6.1
  N10: U3.D5_(PWM), J58.pin1
  N11: U3.D6_(PWM), J58.pin2
  N12: U3.D7, J58.pin3
  N13: U3.D9_(PWM), R14.Pin_0
  N14: U3.D10_(PWM), R13.Pin_0
  N15: U3.D11_(PWM), R12.Pin_1
  N16: U3.A2, JP1.2
  N17: U3.A3, JP1.1
  N18: U3.A4, +_-_2.cathode
  N19: U3.A5, +_-_3.cathode
  N20: D4.Pin_1, Q5.C, RL1.COIL1
  N21: +_-.cathode, R1.Pin_1
  N22: +_-.anode, D1.Pin_1, R2.Pin_0, U2.IN, C1.Pin_0, D2.Pin_1, Q10.G, R11.Pin_1
  N23: +_-_2.anode, Q4.Pin_2
  N24: D1.Pin_0, G1.dc_positive, C2.+
  N25: R21.Pin_0, Q5.B
  N26: R21.Pin_1, Q4.Pin_3
  N27: R15.Pin_0, Q2.B
  N28: Q2.C, SIM800L_20MM1.PIN_8
  N29: RL1.A, C_START_STOP.pin2
  N30: RL1.C, RL2.C, C_START_STOP.pin1
  N31: D5.Pin_0, Q6.C, RL2.COIL2
  N32: Q6.B, R20.Pin_1
  N33: R19.Pin_0, Q4.Pin_1, Q3.Pin_1
  N34: R20.Pin_0, Q3.Pin_4
  N35: +_-_3.anode, Q3.Pin_2
  N36: U2.ADJ, R3.Pin_1, R5.Pin_0
  N37: U2.OUT, R3.Pin_0, R4.Pin_1
  N38: U1.ADJ, R9.Pin_0, R10.Pin_1
  N39: U1.IN, D2.Pin_0, Q10.D
  N40: -.pin1, G1.dc_negative, C2.-, ON/OFF.2, ON/OFF.5
  N41: -.pin2, Q10.S, R7.Pin_0, Q1.C
  N42: D3.C, Q1.E
  N43: D3.A, R4.Pin_0
  N44: G1.ac_input_1, TRF_2.2
  N45: G1.ac_input_2, TRF_2.1
  N46: C10.+, R14.Pin_1, Q7.Pin_4
  N47: RL2.B, C_START_STOP.pin3
  N48: C11.+, R13.Pin_1, Q8.Pin_4
  N49: JP2.1, Q7.Pin_2
  N50: JP2.2, Q7.Pin_1
  N51: JP2.3, Q8.Pin_2
  N52: JP2.4, Q8.Pin_1
  N53: R16.Pin_1, SIM800L_20MM1.PIN_7
  N54: R12.Pin_0, Q9.Pin_4
  N55: R_Y.pin1, TRF.1
  N56: R_Y.pin2, TRF.3
  N57: R7.Pin_1, R6.Pin_0, JP1_2.2
  N58: JP1_2.1, R8.Pin_1
  N59: Q1.B, R8.Pin_0
  N60: R11.Pin_0, Q9.Pin_1
  N61: R22.Pin_0, R25.Pin_0, B_Y_R.pin1
  N62: R22.Pin_1, M1.P$2, D6.C
  N63: R23.Pin_0, B_Y_R.pin2
  N64: R23.Pin_1, R27.Pin_0, M1.P$1
  N65: R25.Pin_1, R29.Pin_0, M2.P$1
  N66: R27.Pin_1, JP2_2.2
  N67: R29.Pin_1, JP2_2.4
  N68: R24.Pin_0, B_Y_R.pin3
  N69: R24.Pin_1, M2.P$2, D7.C
  N70: R26.Pin_0, JP2_2.1
  N71: R26.Pin_1, D6.A
  N72: R28.Pin_0, JP2_2.3
  N73: R28.Pin_1, D7.A

notes:
  M-
  RX
  TX
  STX
  SRX
  1
  C
  MOTOR
  l
  FeedBack
  +
  Battery
  J1
  J2
  Krishna
  M Commander

custom parts:
  Graetz Bridge Rectifier: Graetz Bridge Rectifier - znany także jako Mostek Graetz'a :)
