# Fritzing sketch Motor_Feedback (saved by Fritzing 0.9.3b)
circuit board: 3.2126cm x 3.74451cm
breadboards: 1

parts:
  R27 = Resistor [tolerance=±5% resistance=56k package=THT]
  R28 = Resistor [tolerance=±5% resistance=56k package=THT]
  R29 = Resistor [tolerance=±5% resistance=56k package=THT]
  R30 = Resistor [tolerance=±5% resistance=56k package=THT]
  R31 = Resistor [tolerance=±5% resistance=56k package=THT]
  R32 = Resistor [tolerance=±5% resistance=56k package=THT]
  R33 = Resistor [tolerance=±5% resistance=22k package=THT]
  R34 = Resistor [tolerance=±5% resistance=22k package=THT]
  U8 = V18ZA2P [package=v18za2p]
  U9 = V18ZA2P [package=v18za2p]
  D4150 = Diode [package=diode-1n4001]
  D4151 = Diode [package=diode-1n4001]
  J61 = female pin header, 4 pins [form="♀ (female)"]
  J62 = female pin header, 3 pins [form="♀ (female)"]

nets:
  N1: R27.Pin_0, R29.Pin_0, J62.pin3
  N2: R27.Pin_1, U8.P$2, D4150.C
  N3: R28.Pin_0, J62.pin2
  N4: R28.Pin_1, R30.Pin_0, U8.P$1
  N5: R29.Pin_1, R31.Pin_0, U9.P$1
  N6: R30.Pin_1, J61.pin3
  N7: R31.Pin_1, J61.pin1
  N8: R32.Pin_0, J62.pin1
  N9: R32.Pin_1, U9.P$2, D4151.C
  N10: R33.Pin_0, J61.pin4
  N11: R33.Pin_1, D4150.A
  N12: R34.Pin_0, J61.pin2
  N13: R34.Pin_1, D4151.A
