# Fritzing sketch Exntension (saved by Fritzing 0.9.3b)
circuit board: 8.5cm x 11.12cm
breadboards: 1

parts:
  -_+1 = screw terminal, 2 pins
  RECTIFIER1 = screw terminal, 4 pins
  Q2_PNP1 = PNP-Transistor [package="TO92 [THT]"]
  Q1_NPN1 = NPN-Transistor [part_number=2N2222A package="TO92 [THT]"]
  J51 = rounded female pin header, 4 pins [form="♀ (female rounded)"]
  J52 = rounded female pin header, 2 pins [form="♀ (female rounded)"]
  R5 = Resistor [tolerance=±5% resistance=1k package=THT]
  R6 = Resistor [tolerance=±5% resistance=1k package=THT]
  R7 = Resistor [tolerance=±5% resistance=1k package=THT]
  +_-2 = LED - 5mm [color="Red (633nm)" part_number=LED1 package="5 mm [THT]"]
  -_+2 = screw terminal, 2 pins
  RECTIFIER2 = screw terminal, 4 pins
  Q2_PNP2 = PNP-Transistor [package="TO92 [THT]"]
  Q1_NPN2 = NPN-Transistor [part_number=2N2222A package="TO92 [THT]"]
  J53 = rounded female pin header, 4 pins [form="♀ (female rounded)"]
  J54 = rounded female pin header, 2 pins [form="♀ (female rounded)"]
  R8 = Resistor [tolerance=±5% resistance=1k package=THT]
  R9 = Resistor [tolerance=±5% resistance=1k package=THT]
  R10 = Resistor [tolerance=±5% resistance=1k package=THT]
  +_-3 = LED - 5mm [color="Red (633nm)" part_number=LED1 package="5 mm [THT]"]
  -_+3 = screw terminal, 2 pins
  -_+4 = screw terminal, 2 pins
  RECTIFIER3 = screw terminal, 4 pins
  RECTIFIER4 = screw terminal, 4 pins
  Q2_PNP3 = PNP-Transistor [package="TO92 [THT]"]
  Q2_PNP4 = PNP-Transistor [package="TO92 [THT]"]
  Q1_NPN3 = NPN-Transistor [part_number=2N2222A package="TO92 [THT]"]
  Q1_NPN4 = NPN-Transistor [part_number=2N2222A package="TO92 [THT]"]
  J55 = rounded female pin header, 4 pins [form="♀ (female rounded)"]
  J56 = rounded female pin header, 4 pins [form="♀ (female rounded)"]
  J57 = rounded female pin header, 2 pins [form="♀ (female rounded)"]
  J58 = rounded female pin header, 2 pins [form="♀ (female rounded)"]
  R11 = Resistor [tolerance=±5% resistance=1k package=THT]
  R12 = Resistor [tolerance=±5% resistance=1k package=THT]
  R13 = Resistor [tolerance=±5% resistance=1k package=THT]
  R14 = Resistor [tolerance=±5% resistance=1k package=THT]
  R15 = Resistor [tolerance=±5% resistance=1k package=THT]
  R16 = Resistor [tolerance=±5% resistance=1k package=THT]
  +_-4 = LED - 5mm [color="Red (633nm)" part_number=LED1 package="5 mm [THT]"]
  +_-5 = LED - 5mm [color="Red (633nm)" part_number=LED1 package="5 mm [THT]"]

nets:
  N1: -_+1.pin1, RECTIFIER1.pin4
  N2: -_+1.pin2, RECTIFIER1.pin1
  N3: RECTIFIER1.pin2, J52.pin1
  N4: RECTIFIER1.pin3, J52.pin2
  N5: Q2_PNP1.E, J51.pin1, R5.Pin_1
  N6: Q2_PNP1.B, R5.Pin_0, R6.Pin_0
  N7: Q2_PNP1.C, J51.pin3, +_-2.anode
  N8: Q1_NPN1.E, J51.pin4
  N9: Q1_NPN1.B, J51.pin2
  N10: Q1_NPN1.C, R6.Pin_1, R7.Pin_1
  N11: R7.Pin_0, +_-2.cathode
  N12: -_+2.pin1, RECTIFIER2.pin4
  N13: -_+2.pin2, RECTIFIER2.pin1
  N14: RECTIFIER2.pin2, J54.pin1
  N15: RECTIFIER2.pin3, J54.pin2
  N16: Q2_PNP2.E, J53.pin1, R8.Pin_1
  N17: Q2_PNP2.B, R8.Pin_0, R9.Pin_0
  N18: Q2_PNP2.C, J53.pin3, +_-3.anode
  N19: Q1_NPN2.E, J53.pin4
  N20: Q1_NPN2.B, J53.pin2
  N21: Q1_NPN2.C, R9.Pin_1, R10.Pin_1
  N22: R10.Pin_0, +_-3.cathode
  N23: -_+3.pin1, RECTIFIER3.pin4
  N24: -_+3.pin2, RECTIFIER3.pin1
  N25: -_+4.pin1, RECTIFIER4.pin4
  N26: -_+4.pin2, RECTIFIER4.pin1
  N27: RECTIFIER3.pin2, J57.pin1
  N28: RECTIFIER3.pin3, J57.pin2
  N29: RECTIFIER4.pin2, J58.pin1
  N30: RECTIFIER4.pin3, J58.pin2
  N31: Q2_PNP3.E, J56.pin1, R12.Pin_1
  N32: Q2_PNP3.B, R12.Pin_0, R14.Pin_0
  N33: Q2_PNP3.C, J56.pin3, +_-5.anode
  N34: Q2_PNP4.E, J55.pin1, R11.Pin_1
  N35: Q2_PNP4.B, R11.Pin_0, R13.Pin_0
  N36: Q2_PNP4.C, J55.pin3, +_-4.anode
  N37: Q1_NPN3.E, J55.pin4
  N38: Q1_NPN3.B, J55.pin2
  N39: Q1_NPN3.C, R13.Pin_1, R15.Pin_1
  N40: Q1_NPN4.E, J56.pin4
  N41: Q1_NPN4.B, J56.pin2
  N42: Q1_NPN4.C, R14.Pin_1, R16.Pin_1
  N43: R15.Pin_0, +_-4.cathode
  N44: R16.Pin_0, +_-5.cathode
