# Fritzing sketch Extension (saved by Fritzing 0.9.3b)
circuit board: 5.26097cm x 8.46741cm
breadboards: 1

parts:
  R30 = Resistor [tolerance=±5% resistance=56k package=THT]
  R31 = Resistor [tolerance=±5% resistance=22k package=THT]
  R32 = Resistor [tolerance=±5% resistance=56k package=THT]
  R33 = Resistor [tolerance=±5% resistance=22k package=THT]
  D8 = Diode [package=diode-1n4001]
  U10 = MOV [package=v18za2p]
  C11 = Electrolytic Capacitor [capacitance=33µF voltage=25V package="100 mil [THT, electrolytic]"]
  Q8 = Sharp PC817 [package=THT]
  J74 = rounded female pin header, 4 pins [form="♀ (female rounded)"]
  R34 = Resistor [tolerance=±5% resistance=56k package=THT]
  R35 = Resistor [tolerance=±5% resistance=22k package=THT]
  R36 = Resistor [tolerance=±5% resistance=56k package=THT]
  R37 = Resistor [tolerance=±5% resistance=22k package=THT]
  D9 = Diode [package=diode-1n4001]
  U11 = MOV [package=v18za2p]
  J75 = rounded female pin header, 4 pins [form="♀ (female rounded)"]
  C12 = Electrolytic Capacitor [capacitance=33µF voltage=25V package="100 mil [THT, electrolytic]"]
  Q9 = Sharp PC817 [package=THT]

nets:
  N1: R30.Pin_0, J74.pin2
  N2: R30.Pin_1, R31.Pin_0, U10.P$2
  N3: R31.Pin_1, Q8.Pin_1
  N4: R32.Pin_0, J74.pin1
  N5: R32.Pin_1, D8.C, U10.P$1
  N6: R33.Pin_0, Q8.Pin_2
  N7: R33.Pin_1, D8.A
  N8: C11.-, Q8.Pin_3, J74.pin3
  N9: C11.+, Q8.Pin_4, J74.pin4
  N10: R34.Pin_0, J75.pin2
  N11: R34.Pin_1, R35.Pin_0, U11.P$2
  N12: R35.Pin_1, Q9.Pin_1
  N13: R36.Pin_0, J75.pin1
  N14: R36.Pin_1, D9.C, U11.P$1
  N15: R37.Pin_0, Q9.Pin_2
  N16: R37.Pin_1, D9.A
  N17: J75.pin3, C12.-, Q9.Pin_3
  N18: J75.pin4, C12.+, Q9.Pin_4

custom parts:
  MOV: Metal Oxide Varistor
