# Fritzing sketch Motor_Schematic (saved by Fritzing 0.9.3b)
breadboards: 1

parts:
  Load_&_Comm_IC1 = atmega328 [package=dip]
  12V_INPUT = Power plug
  D4 = Schottky Diode [part_number=1N5819 package="300 mil [THT]"]
  +_-1 = LED - 5mm [color="Red (633nm)" package="5 mm [THT]"]
  R18 = Resistor [tolerance=±5% resistance=1k package=THT]
  U4 = Voltage Regulator - Variable [package="TO220 [THT]"]
  R19 = Resistor [tolerance=±5% resistance=4.7k package=THT]
  R20 = Resistor [tolerance=±5% resistance=4.7k package=THT]
  BATTERY = Power plug
  C1 = Ceramic Capacitor [capacitance=100nF package="200 mil [THT, multilayer]"]
  C48 = Resistor [tolerance=±5% resistance=220 package=THT]
  D6 = Schottky Diode [part_number=1N5817 package="300 mil [THT]"]
  U5 = Voltage Regulator - Variable [package="TO220 [THT]"]
  R21 = Resistor [tolerance=±5% resistance=4.7k package=THT]
  R22 = Resistor [tolerance=±5% resistance=4.7k package=THT]
  R23 = Resistor [tolerance=±5% resistance=4.7k package=THT]
  D7 = Schottky Diode [part_number=1N5817 package="300 mil [THT]"]
  C49 = Ceramic Capacitor [capacitance=100nF package="200 mil [THT, multilayer]"]
  C50 = Electrolytic Capacitor [capacitance=1000µF voltage=16V package="300 mil [THT, electrolytic]"]
  C51 = Ceramic Capacitor [capacitance=100nF package="200 mil [THT, multilayer]"]
  XTAL1 = Crystal [frequency="8 MHz" package=THT]
  C52 = Ceramic Capacitor [capacitance=10pF voltage=10V package="200 mil [THT, multilayer]"]
  C53 = Ceramic Capacitor [capacitance=100nF package="200 mil [THT, multilayer]"]
  Q8 = MOSFET-NCHANNEL [package=sot23-3]
  OPC1 = Sharp PC817 [package=THT]
  R24 = Resistor [tolerance=±5% resistance=1k package=THT]
  +_-1_2 = LED - 5mm [color="Red (633nm)" package="5 mm [THT]"]
  OPC2 = Sharp PC817 [package=THT]
  +_-2 = LED - 5mm [color="Red (633nm)" package="5 mm [THT]"]
  T3 = NPN-Transistor [part_number=2N2222A package="TO92 [THT]"]
  R25 = Resistor [tolerance=±5% resistance=1k package=THT]
  T4 = NPN-Transistor [package="TO92 [THT]"]
  R26 = Resistor [tolerance=±5% resistance=1k package=THT]
  NO1 = OMRON PCB Power Relay – G5LE [part_number="G5LE-1\n" package=THT]
  NO2 = OMRON PCB Power Relay – G5LE [part_number="G5LE-1\n" package=THT]
  ON1_ON3 = screw terminal, 3 pins
  R27 = Resistor [tolerance=±5% resistance=4.7k package=THT]
  Transformer_I/P = Header 3 [package=jst-3-pth]
  2_PHASE_AC = screw terminal, 2 pins
  Transformer_O/P = Header 2 [package=jst-2-pth]
  G2 = Graetz Bridge Rectifier [package="DIP (Dual Inline) [THT]"]
  R28 = Resistor [tolerance=±5% resistance=4.7k package=THT]
  R29 = Resistor [tolerance=±5% resistance=4.7k package=THT]
  T5 = NPN-Transistor [package="TO92 [THT]"]
  R30 = Resistor [tolerance=±5% resistance=4.7k package=THT]
  SIM800L_CUSTOM3 = SIM800L_CUSTOM
  C54 = Ceramic Capacitor [capacitance=100nF package="200 mil [THT, multilayer]"]
  T6 = NPN-Transistor [package="TO92 [THT]"]
  R31 = Resistor [tolerance=±5% resistance=4.7k package=THT]
  MOTOR_FEEDBACK_3_PHASE_AC = screw terminal, 3 pins
  C55 = Electrolytic Capacitor [capacitance=1000µF voltage=35V package="300 mil [THT, electrolytic]"]
  U9 = V18ZA2P [package=v18za2p]
  R32 = Resistor [tolerance=±5% resistance=56k package=THT]
  R33 = Resistor [tolerance=±5% resistance=56k package=THT]
  R34 = Resistor [tolerance=±5% resistance=56k package=THT]
  R35 = Resistor [tolerance=±5% resistance=56k package=THT]
  U10 = V18ZA2P [package=v18za2p]
  R36 = Resistor [tolerance=±5% resistance=22k package=THT]
  R37 = Resistor [tolerance=±5% resistance=22k package=THT]
  +_-3 = LED - 5mm [color="Red (633nm)" package="5 mm [THT]"]
  D4151 = Diode [package=diode-1n4148]
  OPC3 = Sharp PC817 [package=THT]
  R38 = Resistor [tolerance=±5% resistance=22k package=THT]
  R39 = Resistor [tolerance=±5% resistance=22k package=THT]
  D4152 = Diode [package=diode-1n4148]
  OPC4 = Sharp PC817 [package=THT]
  +_-4 = LED - 5mm [color="Red (633nm)" package="5 mm [THT]"]
  C56 = Electrolytic Capacitor [capacitance=47µF voltage=20V package="300 mil [THT, electrolytic]"]
  C57 = Electrolytic Capacitor [capacitance=47µF voltage=20V package="300 mil [THT, electrolytic]"]
  R40 = Resistor [tolerance=±5% resistance=1k package=THT]
  R41 = Resistor [tolerance=±5% resistance=1k package=THT]
  OPC5 = Sharp PC817 [package=THT]
  R42 = Resistor [tolerance=±5% resistance=4.7k package=THT]
  R43 = Resistor [tolerance=±5% resistance=4.7k package=THT]
  C58 = Electrolytic Capacitor [capacitance=47µF voltage=16V package="300 mil [THT, electrolytic]"]

nets:
  N1: Load_&_Comm_IC1.RESET, R27.Pin_1
  N2: Load_&_Comm_IC1.D0_(RX), SIM800L_CUSTOM3.PIN_5
  N3: Load_&_Comm_IC1.D1_(TX), SIM800L_CUSTOM3.PIN_4
  N4: Load_&_Comm_IC1.D2, R31.Pin_1
  N5: Load_&_Comm_IC1.D3_(PWM), T6.B
  N6: Load_&_Comm_IC1.D4, R42.Pin_1
  N7: Load_&_Comm_IC1.VCC, Load_&_Comm_IC1.AVCC, Load_&_Comm_IC1.AREF, R27.Pin_0
  N8: Load_&_Comm_IC1.GND#7, C52.1, C53.0
  N9: Load_&_Comm_IC1.XLAT1, XTAL1.pin_0, C52.0
  N10: Load_&_Comm_IC1.XLAT2, XTAL1.pin_1, C53.1
  N11: Load_&_Comm_IC1.D9_(PWM), R41.Pin_1
  N12: Load_&_Comm_IC1.D10_(PWM), R40.Pin_1
  GND: Load_&_Comm_IC1.GND#21, 12V_INPUT.GND, R18.Pin_0, R20.Pin_1, BATTERY.GND, C1.0, C48.Pin_1, R22.Pin_1, C49.0, C50.-, C51.1, T3.E, T4.E, R29.Pin_1, SIM800L_CUSTOM3.PIN_6, C54.0, T6.E, C55.-, OPC3.Pin_3, OPC4.Pin_3, C56.-, C57.-, OPC5.Pin_2, OPC5.Pin_3, C58.-
  N13: Load_&_Comm_IC1.A2, R30.Pin_1
  N14: Load_&_Comm_IC1.A3, R28.Pin_1, R29.Pin_0
  N15: Load_&_Comm_IC1.A4, +_-1_2.cathode
  N16: Load_&_Comm_IC1.A5, +_-2.cathode
  N17: 12V_INPUT.VCC, D4.anode, C55.+
  N18: D4.cathode, +_-1.anode, C1.1, C48.Pin_0, D6.anode, U5.IN, Q8.G, R43.Pin_0
  N19: +_-1.cathode, R18.Pin_1
  N20: U4.ADJ, R19.Pin_1, R20.Pin_0
  N21: U4.OUT, R19.Pin_0, C49.1, C50.+, C51.0, OPC1.Pin_3, R24.Pin_0, OPC2.Pin_3, NO1.COIL1, NO2.COIL1, SIM800L_CUSTOM3.PIN2, C54.1, C58.+
  N22: U4.IN, D6.cathode, Q8.S
  N23: BATTERY.VCC, R28.Pin_0, T5.C
  N24: U5.ADJ, R21.Pin_1, R22.Pin_0
  N25: U5.OUT, R21.Pin_0, R23.Pin_0
  N26: R23.Pin_1, D7.anode
  N27: D7.cathode, Q8.D, T5.E
  N28: OPC1.Pin_1, R24.Pin_1, OPC2.Pin_1
  N29: OPC1.Pin_2, +_-1_2.anode
  N30: OPC1.Pin_4, R25.Pin_1
  N31: OPC2.Pin_2, +_-2.anode
  N32: OPC2.Pin_4, R26.Pin_1
  N33: T3.B, R26.Pin_0
  N34: T3.C, NO2.COIL2
  N35: R25.Pin_0, T4.B
  N36: T4.C, NO1.COIL2
  N37: NO1.C, NO2.C, ON1_ON3.pin3
  N38: NO1.B, ON1_ON3.pin2
  N39: NO2.A, ON1_ON3.pin1
  N40: Transformer_I/P.1, 2_PHASE_AC.pin2
  N41: Transformer_I/P.3, 2_PHASE_AC.pin1
  N42: Transformer_O/P.1, G2.ac_input_1
  N43: Transformer_O/P.2, G2.ac_input_2
  N44: T5.B, R30.Pin_0
  N45: SIM800L_CUSTOM3.PIN_7, R31.Pin_0
  N46: SIM800L_CUSTOM3.PIN_8, T6.C
  N47: MOTOR_FEEDBACK_3_PHASE_AC.pin1, R32.Pin_1, R34.Pin_1
  N48: MOTOR_FEEDBACK_3_PHASE_AC.pin2, R33.Pin_1
  N49: MOTOR_FEEDBACK_3_PHASE_AC.pin3, R35.Pin_1
  N50: U9.P$1, R32.Pin_0, R36.Pin_1
  N51: U9.P$2, R33.Pin_0, D4151.C
  N52: R34.Pin_0, U10.P$1, R38.Pin_1
  N53: R35.Pin_0, U10.P$2, D4152.C
  N54: R36.Pin_0, +_-3.anode
  N55: R37.Pin_0, OPC3.Pin_2
  N56: R37.Pin_1, D4151.A
  N57: +_-3.cathode, OPC3.Pin_1
  N58: OPC3.Pin_4, C57.+, R40.Pin_0
  N59: R38.Pin_0, +_-4.anode
  N60: R39.Pin_0, OPC4.Pin_2
  N61: R39.Pin_1, D4152.A
  N62: OPC4.Pin_1, +_-4.cathode
  N63: OPC4.Pin_4, C56.+
  N64: OPC5.Pin_1, R43.Pin_1
  N65: OPC5.Pin_4, R42.Pin_0

custom parts:
  Graetz Bridge Rectifier: Graetz Bridge Rectifier - znany także jako Mostek Graetz'a :)
